# Fritzing sketch CharacterLCD_Pi2_W10 (saved by Fritzing 0.9.2b)
breadboards: 1

parts:
  J1 = Cobbler Plus
  U1 = LCD-16X2 [package=lcd-16x2]
  R1 = Trimmer Potentiometer [maximum_resistance=10kΩ package=THT]
  R2 = Resistor [tolerance=±5% resistance=220 package=THT]

nets:
  N1: J1.#4, U1.DB0
  N2: J1.TXD, U1.DB1
  N3: J1.#22, U1.DB2
  N4: J1.#23, U1.DB3
  N5: J1.3.3V, U1.DB4
  N6: J1.MOSI, U1.DB5
  N7: J1.MISO, U1.VDD, R1.leg2, R2.Pin_0
  N8: J1.SCLK, U1.VSS, U1.R_W, U1.K, R1.leg1
  N9: J1.CE1, U1.DB6
  N10: U1.VO, R1.wiper
  N11: U1.A, R2.Pin_1

custom parts:
  Cobbler Plus: The Cobbler Plus is an add on prototyping board from Adafruit specifically designed for the Raspberry Pi B+ that can break out all those tasty power, GPIO, I2C and SPI pins from the 40-pin header onto a solderless breadboard. This set will make "cobbling together" prototypes with the Pi super easy. The Cobbler Plus can plug into any solderless breadboard.
